// Logisim project EP2.circ as structural Verilog: 10 circuits, main circuit teste
module teste (
  input  in_1,
  input  in_2,
  input  in_3,
  input  in_4,
  output [15:0] out_5,
  output [15:0] out_6
);

  wire clock_1_out;
  wire [7:0] pc_1_output_address;
  wire [15:0] ram_1_data;

  Clock clock_1 (.out(clock_1_out));
  PC pc_1 (.Reset(in_1), .Counter_UP(clock_1_out), .Output_Address(pc_1_output_address));  // open: Set, Input_Address
  RAM #(.dataWidth(16)) ram_1 (
    .addr(pc_1_output_address), .data(ram_1_data), .sel(in_2), .ld(in_3), .clr(in_4));  // open: clk
  IR ir_1 (
    .\Código (ram_1_data[7:0]), .Set(clock_1_out), .\Endereço (ram_1_data[15:8]), .Output(out_5));  // open: Reset
  ACC acc_1 (.Input(ram_1_data), .Output(out_6), .Set(clock_1_out));  // open: Reset
endmodule

module PC (
  input  [7:0] Input_Address,
  input  Set,
  input  Reset,
  input  Counter_UP,
  output [7:0] Output_Address
);

  wire and_1_out, and_2_out, and_3_out, and_4_out, and_5_out, and_6_out, and_7_out, and_8_out, and_9_out,
       and_10_out, and_11_out, and_12_out, and_13_out, and_14_out, and_15_out, and_16_out, j_k_ff_1_qn,
       j_k_ff_2_qn, j_k_ff_3_qn, j_k_ff_4_qn, j_k_ff_5_qn, j_k_ff_6_qn, j_k_ff_7_qn, or_1_out, or_2_out,
       or_3_out, or_4_out, or_5_out, or_6_out, or_7_out, or_8_out;

  and and_1 (and_1_out, Set, ~Input_Address[0]);  // AND_Gate
  and and_2 (and_2_out, Set, Input_Address[0]);
  or or_1 (or_1_out, Reset, and_1_out);
  J_K_Flip_Flop j_k_ff_1 (
    .J(1'b1), .clk(Counter_UP), .K(1'b1), .Q(Output_Address[0]), .Qn(j_k_ff_1_qn), .preset(and_2_out),
    .en(1'b1), .reset(or_1_out));
  and and_3 (and_3_out, Set, ~Input_Address[1]);  // AND_Gate
  and and_4 (and_4_out, Set, Input_Address[1]);
  and and_5 (and_5_out, Set, Input_Address[2]);
  or or_2 (or_2_out, Reset, and_3_out);
  J_K_Flip_Flop j_k_ff_2 (
    .J(1'b1), .clk(j_k_ff_1_qn), .K(1'b1), .Q(Output_Address[1]), .Qn(j_k_ff_2_qn), .preset(and_4_out),
    .en(1'b1), .reset(or_2_out));
  and and_6 (and_6_out, Set, ~Input_Address[2]);  // AND_Gate
  and and_7 (and_7_out, Set, Input_Address[3]);
  or or_3 (or_3_out, Reset, and_6_out);
  J_K_Flip_Flop j_k_ff_3 (
    .J(1'b1), .clk(j_k_ff_2_qn), .K(1'b1), .Q(Output_Address[2]), .Qn(j_k_ff_3_qn), .preset(and_5_out),
    .en(1'b1), .reset(or_3_out));
  and and_8 (and_8_out, Set, Input_Address[4]);
  and and_9 (and_9_out, Set, ~Input_Address[3]);  // AND_Gate
  or or_4 (or_4_out, Reset, and_9_out);
  or or_5 (or_5_out, Reset, and_11_out);
  J_K_Flip_Flop j_k_ff_4 (
    .J(1'b1), .clk(j_k_ff_3_qn), .K(1'b1), .Q(Output_Address[3]), .Qn(j_k_ff_4_qn), .preset(and_7_out),
    .en(1'b1), .reset(or_4_out));
  and and_10 (and_10_out, Set, ~Input_Address[5]);  // AND_Gate
  and and_11 (and_11_out, Set, ~Input_Address[4]);  // AND_Gate
  and and_12 (and_12_out, Set, Input_Address[5]);
  or or_6 (or_6_out, Reset, and_10_out);
  and and_13 (and_13_out, Set, Input_Address[6]);
  and and_14 (and_14_out, Set, ~Input_Address[6]);  // AND_Gate
  or or_7 (or_7_out, Reset, and_14_out);
  J_K_Flip_Flop j_k_ff_5 (
    .J(1'b1), .clk(j_k_ff_4_qn), .K(1'b1), .Q(Output_Address[4]), .Qn(j_k_ff_5_qn), .preset(and_8_out),
    .en(1'b1), .reset(or_5_out));
  and and_15 (and_15_out, Set, ~Input_Address[7]);  // AND_Gate
  and and_16 (and_16_out, Set, Input_Address[7]);
  or or_8 (or_8_out, Reset, and_15_out);
  J_K_Flip_Flop j_k_ff_6 (
    .J(1'b1), .clk(j_k_ff_5_qn), .K(1'b1), .Q(Output_Address[5]), .Qn(j_k_ff_6_qn), .preset(and_12_out),
    .en(1'b1), .reset(or_6_out));
  J_K_Flip_Flop j_k_ff_7 (
    .J(1'b1), .clk(j_k_ff_6_qn), .K(1'b1), .Q(Output_Address[6]), .Qn(j_k_ff_7_qn), .preset(and_13_out),
    .en(1'b1), .reset(or_7_out));
  J_K_Flip_Flop j_k_ff_8 (
    .J(1'b1), .clk(j_k_ff_7_qn), .K(1'b1), .Q(Output_Address[7]), .preset(and_16_out), .en(1'b1),
    .reset(or_8_out));  // open: Qn
endmodule

module ACC (
  input  [15:0] Input,
  input  Set,
  input  Reset,
  output [15:0] Output
);

  Register #(.width(16)) register_1 (.D(Input), .en(1'b1), .Q(Output), .clk(Set), .clr(Reset));
endmodule

module IR (
  input  [7:0] \Código ,
  input  Set,
  input  Reset,
  input  [7:0] \Endereço ,
  output [15:0] Output
);

  Register register_1 (.D(\Código ), .en(1'b1), .Q(Output[7:0]), .clk(Set), .clr(Reset));
  Register register_2 (.D(\Endereço ), .en(1'b1), .Q(Output[15:8]), .clk(Set), .clr(Reset));
endmodule

module CTRL (
  input  [15:0] RAM_OUT,
  input  [7:0] PC_Address_OUT,
  input  [15:0] ACC_OUT,
  input  [15:0] IR_OUT,
  input  Reboot,
  output RAM_CLR,
  output ACC_SET,
  output Clock,
  output PC_RESET,
  output ACC_RESET,
  output IR_RESET,
  output PC_SET,
  output [7:0] IR_Address,
  output [7:0] PC_Address_IN,
  output [7:0] IR_Codigo,
  output RAM_LD
);

  wire CLOCK_t, cmp_1_out_3, cmp_2_out_3, cmp_3_p1, NOP, STOP;
  wire [7:0] undriven, undriven_2;

  Clock clock_1 (.out(CLOCK_t));
  and and_1 (Clock, 1'b1, 1'b1, 1'b1, NOP, STOP, CLOCK_t, ~Reboot);  // AND_Gate
  CMP cmp_1 (.in_1(IR_OUT[7:0]), .in_2(8'h32), .out_3(cmp_1_out_3));
  D_Flip_Flop d_ff_1 (.Qn(STOP), .preset(cmp_2_out_3), .reset(Reboot));  // open: clk, D, Q, en
  CMP cmp_2 (.in_1(IR_OUT[7:0]), .in_2(8'h46), .out_3(cmp_2_out_3));
  not not_1 (NOP, cmp_1_out_3);
  // AND_Gate and_2 has open pins: in0=Reboot, in1=CLOCK_t, out=open
  // CMP cmp_3: pin names not known; wires that end beside it: cmp_3_p1, 8'hb, ACC_SET
  CMP cmp_4 (.in_1(undriven), .in_2(8'h33));  // open: out_3
  CMP cmp_5 (.in_1(undriven_2), .in_2(8'hc));  // open: out_3

  assign ACC_RESET = Reboot;
  assign IR_RESET = Reboot;
  assign PC_RESET = Reboot;

  // Other names for the same wires on the sheet: COD[7:0] = IR_OUT[7:0]; ADD[7:0] = IR_OUT[15:8]

  // Notes on the sheet:
  //   Parada - 70
endmodule

module teste2 (
  input  in_1,
  input  in_2,
  input  in_3,
  input  in_4,
  input  in_5,
  output [7:0] out_6,
  output [7:0] out_7,
  output [7:0] out_8,
  output [7:0] out_9,
  output [7:0] out_10,
  output [15:0] out_11,
  output [7:0] out_12
);

  wire button_1_out, ctrl_1_clock, ctrl_1_ir_reset, ctrl_1_pc_reset, ctrl_1_pc_set;
  wire [15:0] buffer_1_out, ir_1_output;

  Button button_1 (.out(button_1_out));
  CTRL ctrl_1 (
    .PC_SET(ctrl_1_pc_set), .PC_RESET(ctrl_1_pc_reset), .ACC_SET(in_1), .IR_RESET(ctrl_1_ir_reset),
    .IR_Address(out_7), .IR_Codigo(out_10), .IR_OUT(ir_1_output), .Clock(ctrl_1_clock), .Reboot(button_1_out));  // open: RAM_OUT, RAM_CLR, PC_Address_IN, ACC_RESET, PC_Address_OUT, ACC_OUT, RAM_LD
  RAM #(.dataWidth(16)) ram_1 (.addr(out_12), .data({out_8, out_6}), .sel(in_3), .clk(in_4), .ld(in_5));  // open: clr
  PC pc_1 (
    .Set(ctrl_1_pc_set), .Reset(ctrl_1_pc_reset), .Counter_UP(ctrl_1_clock), .Input_Address(out_9),
    .Output_Address(out_12));
  ACC acc_1 (.Input({out_8, out_6}));  // open: Output, Set, Reset
  IR ir_1 (.\Código (out_6), .Set(ctrl_1_clock), .Reset(ctrl_1_ir_reset), .\Endereço (out_8), .Output(ir_1_output));
  assign buffer_1_out = ir_1_output;  // Buffer buffer_1, 16 bits wide
  assign {out_9, out_11[7:0]} = buffer_1_out;  // Buffer buffer_2, 16 bits wide

  assign out_11[15:8] = out_9;
endmodule

module SPL168 (
  input  [15:0] in_1,
  output [7:0] out_2,
  output [7:0] out_3
);


  assign out_2 = in_1[7:0];
  assign out_3 = in_1[15:8];
endmodule

module MRG816 (
  input  [7:0] in_1,
  input  [7:0] in_2,
  output [15:0] out_3
);


  assign out_3 = {in_2, in_1};
endmodule

module CMP (
  input  [7:0] in_1,
  input  [7:0] in_2,
  output out_3
);

  wire [7:0] xnor_1_out;

  assign xnor_1_out = ~(in_1 ^ in_2);  // XNOR_Gate xnor_1, 8 bits wide
  and and_1 (out_3, xnor_1_out[0], xnor_1_out[1], xnor_1_out[2], xnor_1_out[3], xnor_1_out[4], xnor_1_out[5], xnor_1_out[6], xnor_1_out[7]);
endmodule

module main (
);

  wire ACC_EN, CLOCK, CU, IR_EN, PC_SET, RAM_CLOCK, RAM_LOAD, RESET;
  wire [7:0] PC_IN, PC_OUT, RAM_ADDR;
  wire [15:0] ACC_IN, ACC_OUT, IR_IN, IR_OUT, ram_1_data, RAM_OUT;

  CTRL ctrl_1 ();  // open: RAM_OUT, RAM_CLR, PC_SET, PC_RESET, PC_Address_IN, ACC_SET, ACC_RESET, IR_RESET, IR_Address, IR_Codigo, PC_Address_OUT, ACC_OUT, IR_OUT, RAM_LD, Clock, Reboot
  Register #(.width(16)) ACC (.D(ACC_IN), .en(ACC_EN), .Q(ACC_OUT), .clk(CLOCK), .clr(RESET));
  RAM #(.dataWidth(16)) ram_1 (
    .addr(RAM_ADDR), .data(ram_1_data), .sel(1'b1), .clk(RAM_CLOCK), .ld(RAM_LOAD));  // open: clr
  Button button_1 (.out(RESET));
  Transistor #(.width(16)) transistor_1 (.in(ACC_OUT), .out(ram_1_data), .gate(RAM_LOAD));
  Transistor #(.\type ("n"), .width(16)) transistor_2 (.in(ram_1_data), .out(RAM_OUT), .gate(RAM_LOAD));
  Clock clock_1 (.out(CLOCK));
  Register #(.width(16)) IR (.D(IR_IN), .en(IR_EN), .Q(IR_OUT), .clk(CLOCK), .clr(RESET));
  PC pc_1 (.Set(PC_SET), .Reset(RESET), .Counter_UP(CU), .Input_Address(PC_IN), .Output_Address(PC_OUT));

  // Notes on the sheet:
  //   RAM
endmodule
