// Logisim project EP3.circ as structural Verilog: 6 circuits, main circuit main
module PC (
  input  [7:0] Input_Address,
  input  Set,
  input  Reset,
  input  Counter_UP,
  output [7:0] Output_Address
);

  wire and_1_out, and_2_out, and_3_out, and_4_out, and_5_out, and_6_out, and_7_out, and_8_out, and_9_out,
       and_10_out, and_11_out, and_12_out, and_13_out, and_14_out, and_15_out, and_16_out, j_k_ff_1_qn,
       j_k_ff_2_qn, j_k_ff_3_qn, j_k_ff_4_qn, j_k_ff_5_qn, j_k_ff_6_qn, j_k_ff_7_qn, or_1_out, or_2_out,
       or_3_out, or_4_out, or_5_out, or_6_out, or_7_out, or_8_out;

  and and_1 (and_1_out, Set, Input_Address[0]);
  J_K_Flip_Flop j_k_ff_1 (
    .J(1'b1), .clk(Counter_UP), .K(1'b1), .Q(Output_Address[0]), .Qn(j_k_ff_1_qn), .preset(and_1_out),
    .en(1'b1), .reset(or_2_out));
  and and_2 (and_2_out, Set, ~Input_Address[0]);  // AND_Gate
  and and_3 (and_3_out, Set, Input_Address[1]);
  or or_1 (or_1_out, Reset, and_6_out);
  or or_2 (or_2_out, Reset, and_2_out);
  J_K_Flip_Flop j_k_ff_2 (
    .J(1'b1), .clk(j_k_ff_1_qn), .K(1'b1), .Q(Output_Address[1]), .Qn(j_k_ff_2_qn), .preset(and_3_out),
    .en(1'b1), .reset(or_1_out));
  and and_4 (and_4_out, Set, ~Input_Address[2]);  // AND_Gate
  and and_5 (and_5_out, Set, Input_Address[2]);
  and and_6 (and_6_out, Set, ~Input_Address[1]);  // AND_Gate
  or or_3 (or_3_out, Reset, and_4_out);
  and and_7 (and_7_out, Set, Input_Address[3]);
  and and_8 (and_8_out, Set, ~Input_Address[3]);  // AND_Gate
  or or_4 (or_4_out, Reset, and_8_out);
  J_K_Flip_Flop j_k_ff_3 (
    .J(1'b1), .clk(j_k_ff_2_qn), .K(1'b1), .Q(Output_Address[2]), .Qn(j_k_ff_3_qn), .preset(and_5_out),
    .en(1'b1), .reset(or_3_out));
  and and_9 (and_9_out, Set, ~Input_Address[4]);  // AND_Gate
  and and_10 (and_10_out, Set, Input_Address[4]);
  or or_5 (or_5_out, Reset, and_9_out);
  J_K_Flip_Flop j_k_ff_4 (
    .J(1'b1), .clk(j_k_ff_3_qn), .K(1'b1), .Q(Output_Address[3]), .Qn(j_k_ff_4_qn), .preset(and_7_out),
    .en(1'b1), .reset(or_4_out));
  and and_11 (and_11_out, Set, ~Input_Address[5]);  // AND_Gate
  and and_12 (and_12_out, Set, Input_Address[5]);
  or or_6 (or_6_out, Reset, and_11_out);
  J_K_Flip_Flop j_k_ff_5 (
    .J(1'b1), .clk(j_k_ff_4_qn), .K(1'b1), .Q(Output_Address[4]), .Qn(j_k_ff_5_qn), .preset(and_10_out),
    .en(1'b1), .reset(or_5_out));
  and and_13 (and_13_out, Set, ~Input_Address[6]);  // AND_Gate
  and and_14 (and_14_out, Set, Input_Address[7]);
  and and_15 (and_15_out, Set, Input_Address[6]);
  or or_7 (or_7_out, Reset, and_13_out);
  J_K_Flip_Flop j_k_ff_6 (
    .J(1'b1), .clk(j_k_ff_5_qn), .K(1'b1), .Q(Output_Address[5]), .Qn(j_k_ff_6_qn), .preset(and_12_out),
    .en(1'b1), .reset(or_6_out));
  and and_16 (and_16_out, Set, ~Input_Address[7]);  // AND_Gate
  or or_8 (or_8_out, Reset, and_16_out);
  J_K_Flip_Flop j_k_ff_7 (
    .J(1'b1), .clk(j_k_ff_6_qn), .K(1'b1), .Q(Output_Address[6]), .Qn(j_k_ff_7_qn), .preset(and_15_out),
    .en(1'b1), .reset(or_7_out));
  J_K_Flip_Flop j_k_ff_8 (
    .J(1'b1), .clk(j_k_ff_7_qn), .K(1'b1), .Q(Output_Address[7]), .preset(and_14_out), .en(1'b1),
    .reset(or_8_out));  // open: Qn
endmodule

module CTRL (
  input  Entradas,
  input  in_2,
  input  [15:0] IR_OUT,
  input  [7:0] in_4,
  input  [15:0] ACC_OUT,
  input  [15:0] INN,
  output RAM_CLOCK,
  output RAM_LD,
  output CU,
  output IR_EN,
  output ACC_EN,
  output PC_SET,
  output PRN_EN,
  output [7:0] PC_IN,
  output [7:0] RAM_ADDRESS,
  output [2:0] S,
  output out_17,
  output OP,
  output [15:0] OUT
);

  wire ADD, and_7_out, clock_1_out, cmp16_1_out_4, cmp16_2_out_3, cmp16_3_out_4, cmp16_4_out_3,
       cmp16_5_out_5, cmp16_6_out_5, cmp_3_out_4, cmp_4_out_4, cmp_5_out_4, cmp_6_out_4, cmp_7_out_4,
       cmp_8_out_4, DIV, ENABLE, JDZ, JEQ, JGE, JGT, JLE, JLT, JMP, LDA, MUL, NOP, or_4_out, REM, STA, STOP,
       SUB;
  wire [1:0] counter_1_q;

  CMP cmp_1 (.in_1(IR_OUT[7:0]), .in_2(8'hb), .out_4(LDA), .Enable(ENABLE));
  CMP cmp_2 (.in_1(IR_OUT[7:0]), .in_2(8'h32), .out_4(NOP), .Enable(ENABLE));
  CMP cmp_3 (.in_1(IR_OUT[7:0]), .in_2(8'h34), .out_4(cmp_3_out_4), .Enable(ENABLE));
  CMP cmp_4 (.in_1(IR_OUT[7:0]), .in_2(8'h35), .out_4(cmp_4_out_4), .Enable(ENABLE));
  CMP cmp_5 (.in_1(IR_OUT[7:0]), .in_2(8'h36), .out_4(cmp_5_out_4), .Enable(ENABLE));
  CMP cmp_6 (.in_1(IR_OUT[7:0]), .in_2(8'h37), .out_4(cmp_6_out_4), .Enable(ENABLE));
  CMP cmp_7 (.in_1(IR_OUT[7:0]), .in_2(8'h38), .out_4(cmp_7_out_4), .Enable(ENABLE));
  CMP cmp_8 (.in_1(IR_OUT[7:0]), .in_2(8'h39), .out_4(cmp_8_out_4), .Enable(ENABLE));
  CMP cmp_9 (.in_1(IR_OUT[7:0]), .in_2(8'h33), .out_4(JMP), .Enable(ENABLE));
  CMP16 cmp16_1 (.in_1(ACC_OUT), .in_2({16{1'b0}}), .out_4(cmp16_1_out_4));  // open: out_3, out_5
  CMP16 cmp16_2 (.in_1(ACC_OUT), .in_2({16{1'b0}}), .out_3(cmp16_2_out_3));  // open: out_4, out_5
  CMP16 cmp16_3 (.in_1(ACC_OUT), .in_2({16{1'b0}}), .out_4(cmp16_3_out_4));  // open: out_3, out_5
  CMP16 cmp16_4 (.in_1(ACC_OUT), .in_2({16{1'b0}}), .out_3(cmp16_4_out_3));  // open: out_4, out_5
  CMP16 cmp16_5 (.in_1(ACC_OUT), .in_2({16{1'b0}}), .out_5(cmp16_5_out_5));  // open: out_3, out_4
  CMP16 cmp16_6 (.in_1(ACC_OUT), .in_2({16{1'b0}}), .out_5(cmp16_6_out_5));  // open: out_3, out_4
  CMP cmp_10 (.in_1(IR_OUT[7:0]), .in_2(8'hc), .out_4(STA), .Enable(ENABLE));
  CMP cmp_11 (.in_1(IR_OUT[7:0]), .in_2(8'h46), .out_4(STOP), .Enable(ENABLE));
  and and_1 (JLE, cmp_3_out_4, ~cmp16_1_out_4);  // AND_Gate
  and and_2 (JDZ, cmp_4_out_4, ~cmp16_2_out_3);  // AND_Gate
  and and_3 (JGT, cmp_5_out_4, cmp16_3_out_4);
  and and_4 (JEQ, cmp_6_out_4, cmp16_4_out_3);
  and and_5 (JLT, cmp_7_out_4, cmp16_5_out_5);
  and and_6 (JGE, cmp_8_out_4, ~cmp16_6_out_5);  // AND_Gate
  or or_1 (ACC_EN, LDA, OP);
  CMP cmp_12 (.in_1(IR_OUT[7:0]), .in_2(8'h15), .out_4(ADD), .Enable(ENABLE));
  CMP cmp_13 (.in_1(IR_OUT[7:0]), .in_2(8'h16), .out_4(SUB), .Enable(ENABLE));
  CMP cmp_14 (.in_1(IR_OUT[7:0]), .in_2(8'h17), .out_4(MUL), .Enable(ENABLE));
  CMP cmp_15 (.in_1(IR_OUT[7:0]), .in_2(8'h18), .out_4(DIV), .Enable(ENABLE));
  CMP cmp_16 (.in_1(IR_OUT[7:0]), .in_2(8'h19), .out_4(REM), .Enable(ENABLE));
  nor nor_1 (RAM_LD, STA, out_17);
  Transistor #(.\type ("n"), .width(3)) transistor_1 (.in(3'b000), .out(S), .gate(ADD));
  Transistor #(.\type ("n"), .width(3)) transistor_2 (.in(3'b001), .out(S), .gate(SUB));
  Transistor #(.\type ("n"), .width(3)) transistor_3 (.in(3'b010), .out(S), .gate(MUL));
  Transistor #(.\type ("n"), .width(3)) transistor_4 (.in(3'b011), .out(S), .gate(DIV));
  Transistor #(.\type ("n"), .width(3)) transistor_5 (.in(3'b100), .out(S), .gate(REM));
  CMP cmp_17 (.in_1(IR_OUT[7:0]), .in_2(8'h1f), .out_4(out_17), .Enable(ENABLE));
  CMP cmp_18 (.in_1(IR_OUT[7:0]), .in_2(8'h29), .out_4(PRN_EN), .Enable(ENABLE));
  and and_7 (and_7_out, ~STOP, Entradas);  // AND_Gate
  Demultiplexer #(.select(2), .enable("false")) demultiplexer_1 (
    .out0(IR_EN), .out1(CU), .out2(ENABLE), .in(1'b1), .sel(counter_1_q));  // open: out3
  Counter #(.width(2), .max('h2)) counter_1 (
    .Q(counter_1_q), .clk(and_7_out), .clr(in_2));  // open: load, D, count, carry
  Transistor #(.width(8)) transistor_6 (.in(in_4), .out(RAM_ADDRESS), .gate(or_4_out));
  Transistor #(.\type ("n")) transistor_7 (.in(clock_1_out), .out(RAM_CLOCK), .gate(ENABLE));
  Clock clock_1 (.out(clock_1_out));
  or or_2 (PC_SET, JMP, JLE, JDZ, JGT, JEQ, JLT, JGE);
  or or_3 (OP, ADD, SUB, MUL, DIV, REM);
  or or_4 (or_4_out, LDA, STA, PRN_EN, out_17, OP);
  Transistor #(.\type ("n"), .width(8)) transistor_8 (.in(IR_OUT[15:8]), .out(RAM_ADDRESS), .gate(or_4_out));

  assign PC_IN = IR_OUT[15:8];

  // Other names for the same wires on the sheet: CLOCK = Entradas; INN_t = out_17; INPUT[15:0] = INN;
  //   COD[7:0] = IR_OUT[7:0]; IR_ADDR[7:0] = IR_OUT[15:8]; JUMP = PC_SET; MATH = OP; OUTPUT[15:0] = OUT;
  //   PC_OUT[7:0] = in_4; PRN = PRN_EN; RESET = in_2

  // Notes on the sheet:
  //   LDA - 11
  //   NOP - 50
  //   Jumps
  //   JMP - 51
  //   JLE - 52
  //   JDZ - 53
  //   JGT - 54
  //   JEQ - 55
  //   JLT - 56
  //   JGE - 57
  //   Instruções
  //   STA - 12
  //   STP - 70
  //   Saídas
  //   Aritimética
  //   ADD - 21
  //   SUB - 22
  //   MUL - 23
  //   DIV - 24
  //   REM - 25
  //   INN - 31
  //   PRN - 41
  //   Ciclo de Instrução
  //   JMP - PC_SET
  //   IS_OPERATION
  //   Selecionar acesso à RAM
endmodule

module CMP (
  input  [7:0] in_1,
  input  [7:0] in_2,
  input  Enable,
  output out_4
);

  wire and_1_out;
  wire [7:0] xnor_1_out;

  assign xnor_1_out = ~(in_1 ^ in_2);  // XNOR_Gate xnor_1, 8 bits wide
  and and_1 (and_1_out, xnor_1_out[0], xnor_1_out[1], xnor_1_out[2], xnor_1_out[3], xnor_1_out[4], xnor_1_out[5], xnor_1_out[6], xnor_1_out[7]);
  and and_2 (out_4, and_1_out, Enable);
endmodule

module main (
  input  [2:0] in_1,
  input  [15:0] in_2,
  output [7:0] out_3,
  output [15:0] out_4,
  output [7:0] out_5,
  output [15:0] out_6,
  output [15:0] out_7,
  output [15:0] out_8
);

  wire ACC_EN, CLOCK, CU, IR_EN, keyboard_1_avail, OP, PC_SET, PRN_EN, RAM_CLOCK, RAM_LOAD, RESET, SCAN;
  wire [2:0] S;
  wire [6:0] keyboard_1_data;
  wire [7:0] RAM_ADDR;
  wire [15:0] IR_OUT, OUT, Output_q, ram_1_data, transistor_1_out, transistor_5_out;

  Button button_1 (.out(RESET));
  Clock #(.highDuration(2)) clock_1 (.out(CLOCK));
  Register #(.width(16)) Output (.D(out_8), .en(PRN_EN), .Q(Output_q), .clk(CLOCK), .clr(RESET));
  RAM #(.dataWidth(16)) ram_1 (
    .addr(RAM_ADDR), .data(ram_1_data), .sel(1'b1), .clk(RAM_CLOCK), .ld(RAM_LOAD));  // open: clr
  Hex_Digit_Display hex_digit_display_1 (.value(Output_q[15:12]));  // open: dp
  Hex_Digit_Display hex_digit_display_2 (.value(Output_q[11:8]));  // open: dp
  CTRL ctrl_1 (
    .IR_OUT(IR_OUT), .RAM_LD(RAM_LOAD), .IR_EN(IR_EN), .CU(CU), .RAM_CLOCK(RAM_CLOCK), .Entradas(CLOCK),
    .in_2(RESET), .PC_IN(out_3), .PC_SET(PC_SET), .RAM_ADDRESS(RAM_ADDR), .in_4(out_5), .ACC_EN(ACC_EN),
    .ACC_OUT(out_4), .S(S), .OP(OP), .INN(in_2), .OUT(OUT), .out_17(SCAN), .PRN_EN(PRN_EN));
  Transistor #(.gate("br"), .width(16)) transistor_1 (.in(out_4), .out(transistor_1_out), .gate(SCAN));
  Transistor #(.width(16)) transistor_2 (.in(transistor_1_out), .out(ram_1_data), .gate(RAM_LOAD));
  Transistor #(.\type ("n"), .width(16)) transistor_3 (.in(in_2), .out(transistor_1_out), .gate(SCAN));
  Transistor #(.\type ("n"), .gate("br"), .width(16)) transistor_4 (.in(ram_1_data), .out(out_8), .gate(RAM_LOAD));
  Hex_Digit_Display hex_digit_display_3 (.value(Output_q[7:4]));  // open: dp
  Hex_Digit_Display hex_digit_display_4 (.value(Output_q[3:0]));  // open: dp
  Key_interpreter key_interpreter_1 ();  // open: Clock_out, Start, Reset, out_5, in_3
  Keyboard #(.buflen(4)) keyboard_1 (
    .re(1'b1), .clr(RESET), .avail(keyboard_1_avail), .data(keyboard_1_data));  // open: clk
  Transistor #(.width(16)) transistor_5 (.in(out_8), .out(transistor_5_out), .gate(OP));
  Transistor #(.\type ("n"), .width(16)) transistor_6 (.in(out_6), .out(transistor_5_out), .gate(OP));
  Register #(.width(16)) ACC (.D(transistor_5_out), .en(ACC_EN), .Q(out_4), .clk(CLOCK), .clr(RESET));
  PC pc_1 (.Set(PC_SET), .Reset(RESET), .Counter_UP(CU), .Input_Address(out_3), .Output_Address(out_5));
  Transistor #(.\type ("n"), .width(16)) transistor_7 (.in(out_4), .out(out_7), .gate(RAM_LOAD));
  Register #(.width(16)) IR (.D(out_8), .en(IR_EN), .Q(IR_OUT), .clk(CLOCK), .clr(RESET));
  ALU alu_1 (.A(out_7), .B(out_8), .S(in_1), .out_4(out_6));  // open: Overflow, div_0

  // Other names for the same wires on the sheet: ACC_OUT[15:0] = out_4; ALU_OUT[15:0] = out_6; INN[15:0] = in_2;
  //   PC_IN[7:0] = out_3; PC_OUT[7:0] = out_5; RAM_OUT[15:0] = out_8

  // Notes on the sheet:
  //   Início
  //   RAM
endmodule

module CMP16 (
  input  [15:0] in_1,
  input  [15:0] in_2,
  output out_3,
  output out_4,
  output out_5
);

  wire [14:0] sub_1_resultado;
  wire [15:0] xnor_1_out;

  assign xnor_1_out = ~(in_1 ^ in_2);  // XNOR_Gate xnor_1, 16 bits wide
  Sub sub_1 (.Minuendo(in_1), .Subtraendo(in_2), .Resultado({out_5, sub_1_resultado}));  // open: Overflow
  and and_1 (out_3, xnor_1_out[0], xnor_1_out[1], xnor_1_out[2], xnor_1_out[3], xnor_1_out[4], xnor_1_out[5], xnor_1_out[6], xnor_1_out[7], xnor_1_out[8], xnor_1_out[9], xnor_1_out[10], xnor_1_out[11], xnor_1_out[12], xnor_1_out[13], xnor_1_out[14], xnor_1_out[15]);
  nor nor_1 (out_4, out_3, out_5);
endmodule

module Key_interpreter (
  input  Reset,
  input  Start,
  input  in_3,
  output Clock_out,
  output [6:0] out_5
);

  wire clock_1_out, cmp16_1_out_3, cmp16_3_out_5, cmp16_4_out_4, d_ff_2_q, d_ff_3_q, d_ff_4_q, fim, lendo,
       nor_1_out, SINAL, terminar;
  wire [15:0] IN, sub_1_resultado;

  Clock clock_1 (.out(clock_1_out));
  and and_1 (Clock_out, lendo, clock_1_out);
  CMP16 cmp16_1 (.in_1({{9{1'b0}}, out_5}), .in_2(16'h2d), .out_3(cmp16_1_out_3));  // open: out_4, out_5
  CMP16 cmp16_2 (.in_1({{9{1'b0}}, out_5}), .in_2(16'ha), .out_3(terminar));  // open: out_4, out_5
  CMP16 cmp16_3 (.in_1({{9{1'b0}}, out_5}), .in_2(16'h30), .out_5(cmp16_3_out_5));  // open: out_3, out_4
  CMP16 cmp16_4 (.in_1({{9{1'b0}}, out_5}), .in_2(16'h39), .out_4(cmp16_4_out_4));  // open: out_3, out_5
  T_Flip_Flop t_ff_1 (.clk(cmp16_1_out_3), .T(cmp16_1_out_3), .Q(SINAL), .reset(fim));  // open: Qn, preset, en
  nor nor_1 (nor_1_out, cmp16_3_out_5, cmp16_4_out_4);
  Transistor #(.width(16)) transistor_1 (.in(sub_1_resultado), .out(IN), .gate(nor_1_out));
  Sub sub_1 (.Minuendo({{9{1'b0}}, out_5}), .Subtraendo(16'h30), .Resultado(sub_1_resultado));  // open: Overflow
  D_Flip_Flop d_ff_1 (.Q(lendo), .preset(Start), .reset(fim));  // open: clk, D, Qn, en
  Keyboard keyboard_1 (.clk(Clock_out), .re(lendo), .clr(fim), .data(out_5));  // open: avail
  or or_1 (fim, terminar, Reset);
  D_Flip_Flop d_ff_2 (.clk(Clock_out), .D(in_3), .Q(d_ff_2_q), .reset(Reset));  // open: Qn, preset, en
  D_Flip_Flop d_ff_3 (.clk(Clock_out), .D(d_ff_4_q), .Q(d_ff_3_q), .reset(Reset));  // open: Qn, preset, en
  D_Flip_Flop d_ff_4 (.clk(Clock_out), .D(d_ff_2_q), .Q(d_ff_4_q), .reset(Reset));  // open: Qn, preset, en
  D_Flip_Flop d_ff_5 (.clk(Clock_out), .D(d_ff_3_q), .reset(Reset));  // open: Q, Qn, preset, en

  // Other names for the same wires on the sheet: CLK_OUT = Clock_out; CHAR[6:0] = out_5

  // Notes on the sheet:
  //   Menos
  //   Enter
  //   Numero
endmodule
